# Fritzing sketch ESP06 (saved by Fritzing 0.9.3b)
circuit board: 3.88288cm x 3.74367cm
breadboards: 1

parts:
  C1 = Capacitor Polarized [package=cpol-radial-100uf-25v]
  hc-sr1 = hc-sr04
  DS2 = DS18B20 1-Wire Temperature Sensor [part_number=DS18B20]
  DS1 = DS18B20 1-Wire Temperature Sensor [part_number=DS18B20]
  J1 = female pin header, 2 pins [form="♀ (female)"]
  J2 = female pin header, 2 pins [form="♀ (female)"]
  V3 = DC Power [voltage=5]
  JP4 = Header 3 [package=1x03-1mm-ra]
  R6 = Resistor [tolerance=±5% resistance=10k package="1206 [SMD]"]
  R5 = Resistor [tolerance=±5% resistance=4.7k package="1206 [SMD]"]
  R4 = Resistor [tolerance=±5% resistance=2.2k package="1206 [SMD]"]
  JP2 = Header 6 [package=1x06-smd]
  R3 = Resistor [tolerance=±5% resistance=4.7k package="1206 [SMD]"]
  R2 = Resistor [tolerance=±5% resistance=4.7k package="1206 [SMD]"]
  R1 = Resistor [tolerance=±5% resistance=4.7k package="1206 [SMD]"]
  IC1 = Voltage Regulator LM1117 [part_number=TS1117BCW package=sot223]
  J5 = female pin header, 3 pins [form="♀ (female)"]
  J6 = female pin header, 6 pins [form="♀ (female)"]
  J3 = male pin header, 3 pins [form="♂ (male)" part_number="rst / flash"]
  U1 = ESP8266 WiFi Module [part_number=ESP12f]

nets:
  3.3V: C1.+, R4.Pin_0, R3.Pin_0, R2.Pin_0, R1.Pin_0, IC1.OUT, J5.pin3, J6.pin6, U1.VCC, U1.CH_PD
  N1: C1.-, J1.pin2, R6.Pin_0, IC1.ADJ, J5.pin1, J6.pin1, J3.pin2, U1.GND, U1.GPIO_15
  N2: hc-sr1.VCC, JP2.3
  N3: hc-sr1.Trig, JP2.4
  N4: hc-sr1.Echo, JP2.5
  GND: hc-sr1.GND, DS1.GND, JP2.6
  N5: DS2.GND, JP4.3
  N6: DS2.DQ, JP4.2
  N7: DS2.VDD, JP4.1
  N8: DS1.DQ, JP2.2
  N9: DS1.VDD, JP2.1
  5V: J1.pin1, IC1.IN, J6.pin4
  N10: J2.pin1, V3.V+
  N11: J2.pin2, V3.V-
  GPIO1 -> ECHO: R6.Pin_1, R5.Pin_0, U1.TXD
  N12: R5.Pin_1, J6.pin2
  ONE WIRE: R4.Pin_1, J5.pin2, J6.pin5, U1.GPIO_5
  N13: R3.Pin_1, U1.GPIO_0
  N14: R2.Pin_1, J3.pin3, U1.GPIO_2
  N15: R1.Pin_1, J3.pin1, U1.REST
  GPIO3 -> TRIG: J6.pin3, U1.RXD

notes:
  ESP06
  5V
  echo
  trig
  GND
  3.3V
  1w
  gnd
  rst
  flash
